# Fritzing sketch PCB_PCF8574 (saved by Fritzing 0.9.3b)
circuit board: 2.24825cm x 3.65727cm
breadboards: 1

parts:
  U1 = PCF8574 [package="DIP16 [THT]"]
  S1 = Toggle Switch [package=THT]
  S2 = Toggle Switch [package=THT]
  S3 = Toggle Switch [package=THT]

nets:
  N1: U1.A0, S3.COM
  N2: U1.A1, S2.COM
  N3: U1.A3, S1.COM
  GND: U1.GND, S1.L2, S2.L2, S3.L2
  5V: U1.VCC, S1.L1, S2.L1, S3.L1

notes:
  VCC GND
  PCF8574
